# Fritzing sketch Radio (saved by Fritzing 0.9.3b)
breadboards: 1
perfboards: 1

parts:
  Part1 = Arduino Uno (Rev3)
  U1 = LCD-16X2 [package=lcd-16x2]
  UP = Pushbutton [package="[THT]"]
  DOWN = Pushbutton [package="[THT]"]
  R1 = Resistor [tolerance=±5% resistance=22k package=THT]
  R2 = Resistor [tolerance=±5% resistance=22k package=THT]
  3_5mm_Audio = Audio Jack (TRS) 3.5mm [package="4Ucon 08780 [THT]"]
  ANT = Audio Jack (TRS) 3.5mm [package="4Ucon 08780 [THT]"]  # not connected
  IC1 = IC, DIP package, 10 pins [chip_label=TEA5767]
  VCC_SDA_SCL_GND = female pin header, 4 pins [form="♀ (female)"]
  R3 = Resistor [tolerance=±5% resistance=10k package=THT]
  part = Resistor [tolerance=±5% resistance=10k package=THT]
  C1 = Electrolytic Capacitor [capacitance=22µF package="0807 [SMD, electrolytic]"]  # not connected

nets:
  N1: Part1.A4/SDA, VCC_SDA_SCL_GND.pin3
  N2: Part1.A5/SCL, VCC_SDA_SCL_GND.pin2
  N3: Part1.D11_PWM/MOSI, U1.E
  N4: Part1.D12/MISO, U1.RS
  N5: Part1.D2, U1.DB7
  N6: Part1.D3_PWM, U1.DB6
  N7: Part1.D4, U1.DB5
  N8: Part1.D5_PWM, U1.DB4
  N9: Part1.D6_PWM, DOWN.Pin_1, DOWN.Pin_2, R2.Pin_0
  N10: Part1.D7, UP.Pin_1, UP.Pin_2, R1.Pin_0
  5V: Part1.5V, U1.VDD, U1.R_W, U1.A, UP.Pin_3, UP.Pin_4, DOWN.Pin_3, DOWN.Pin_4, VCC_SDA_SCL_GND.pin4
  GND: Part1.GND, U1.VSS, U1.K, R1.Pin_1, R2.Pin_1, VCC_SDA_SCL_GND.pin1, R3.Pin_1
  N11: U1.VO, part.Pin_1
  N12: 3_5mm_Audio.Tip, IC1.pin4
  N13: R3.Pin_0, part.Pin_0
