# Fritzing sketch MCP3008 (saved by Fritzing 0.9.3b)
breadboards: 1

parts:
  Raspberry_Pi_1 = Raspberry Pi 3 [part_number=RPI-3-V1.2]
  Part1 = Soil Moisture Sensor
  IC1 = IC, DIP package, 16 pins [chip_label="MCP3008 I/P"]

nets:
  3V3: Raspberry_Pi_1.3v3, Raspberry_Pi_1.3V3, Part1.VCC, IC1.pin15, IC1.pin16
  GND: Raspberry_Pi_1.GND, Part1.GND, IC1.pin9, IC1.pin14
  N1: Raspberry_Pi_1.GPIO10, IC1.pin11
  N2: Raspberry_Pi_1.GPIO9, IC1.pin12
  N3: Raspberry_Pi_1.GPIO11, IC1.pin13
  N4: Raspberry_Pi_1.GPIO8, IC1.pin10
  N5: Part1.SIG, IC1.pin1
