# Fritzing sketch HC-SR04-RPi3 (saved by Fritzing 0.9.2b)
breadboards: 1

parts:
  Raspberry_Pi = Raspberry Pi 3
  Part1 = SRF05 Ultrasonic Rangefinder
  R1 = Resistor [tolerance=±5% resistance=4.7k package="0603 [SMD]"]
  R2 = Resistor [tolerance=±5% resistance=10k package="0603 [SMD]"]

nets:
  N1: Raspberry_Pi.GIPO24, R1.Pin_1, R2.Pin_0
  N2: Raspberry_Pi.GIPO23, Part1.Trig
  GND: Raspberry_Pi.GND, Part1.GND, R2.Pin_1
  5V: Raspberry_Pi.5V, Part1.VCC
  N3: Part1.Echo, R1.Pin_0
