# Fritzing sketch MorseCode (saved by Fritzing 0.9.3b)
breadboards: 1

parts:
  Raspberry_Pi_1 = Raspberry Pi 3 [part_number=RPI-3-V1.2]
  LED1 = LEDs [package=led10mm]
  Grove1 = Grove Buzz

nets:
  3V3: Raspberry_Pi_1.3v3, LED1.A, Grove1.VCC
  GND: Raspberry_Pi_1.GND, Grove1.GND
  N1: Raspberry_Pi_1.GPIO5, Grove1.SIG
  N2: Raspberry_Pi_1.GPIO6, LED1.C
