# Fritzing sketch YK04-L298N-Remote-Rover (saved by Fritzing 0.9.2b)
breadboards: 1

parts:
  R1 = Resistor [tolerance=±5% resistance=4.7k package=THT]
  R2 = Resistor [tolerance=±5% resistance=4.7k package=THT]
  R3 = Resistor [tolerance=±5% resistance=4.7k package=THT]
  R4 = Resistor [tolerance=±5% resistance=4.7k package=THT]
  R5 = Resistor [tolerance=±5% resistance=4.7k package=THT]
  R6 = Resistor [tolerance=±5% resistance=10k package=THT]
  R7 = Resistor [tolerance=±5% resistance=10k package=THT]
  R8 = Resistor [tolerance=±5% resistance=10k package=THT]
  R9 = Resistor [tolerance=±5% resistance=10k package=THT]
  R10 = Resistor [tolerance=±5% resistance=10k package=THT]
  Windows_10_IoT_Core = Raspberry Pi 3
  Left_Motor = DC Motor
  Right_Motor = DC Motor
  315MHz_2262/2272-M4_Remote_Control = PT2272-M4 Receiver [chip_label=IC package="DIP (Dual Inline) [THT]"]
  S1 = H-Bridge with L298N
  VCC1 = 4 x AAA Battery Mount

nets:
  N1: R1.Pin_0, 315MHz_2262/2272-M4_Remote_Control.VT
  N2: R1.Pin_1, R6.Pin_0, Windows_10_IoT_Core.GIPO5
  N3: R2.Pin_0, 315MHz_2262/2272-M4_Remote_Control.D3
  N4: R2.Pin_1, R7.Pin_0, Windows_10_IoT_Core.GIPO6
  N5: R3.Pin_0, 315MHz_2262/2272-M4_Remote_Control.D2
  N6: R3.Pin_1, R8.Pin_0, Windows_10_IoT_Core.GIPO13
  N7: R4.Pin_0, 315MHz_2262/2272-M4_Remote_Control.D1
  N8: R4.Pin_1, R9.Pin_0, Windows_10_IoT_Core.GIPO19
  N9: R5.Pin_0, 315MHz_2262/2272-M4_Remote_Control.D0
  N10: R5.Pin_1, R10.Pin_0, Windows_10_IoT_Core.GIPO26
  GND: R6.Pin_1, R7.Pin_1, R8.Pin_1, R9.Pin_1, R10.Pin_1, Windows_10_IoT_Core.GND, 315MHz_2262/2272-M4_Remote_Control.GND, S1.GND, VCC1.-
  N11: Windows_10_IoT_Core.GIPO27, S1.IN4
  N12: Windows_10_IoT_Core.GIPO22, S1.IN3
  N13: Windows_10_IoT_Core.GIPO24, S1.IN2
  N14: Windows_10_IoT_Core.GIPO23, S1.IN1
  5V: Windows_10_IoT_Core.5V, 315MHz_2262/2272-M4_Remote_Control.5V, S1.5V
  N15: Left_Motor.pin_1, S1.M2-02
  N16: Left_Motor.pin_2, S1.M2-01
  N17: Right_Motor.pin_1, S1.M1-01
  N18: Right_Motor.pin_2, S1.M1-02
  N19: S1.12V, VCC1.+
  N20: S1.ENA, S1.ENA-5V
  N21: S1.ENB, S1.ENB-5V

notes:
  Vout = Vin * (R2 / (R1+R2))
  Vout = 5 * (10000 / (4700 + 10000))
  Vout = 3.4v

custom parts:
  H-Bridge with L298N: h-bridge
