# Fritzing sketch YK04-Remote-Door-Controller-Rev (saved by Fritzing 0.9.2b)
breadboards: 1

parts:
  R1 = Resistor [tolerance=±5% resistance=4.7k package=THT]
  R2 = Resistor [tolerance=±5% resistance=10k package=THT]
  Raspberry_Pi_1 = Raspberry Pi 3
  IC1 = PT2272-M4 Receiver [chip_label=IC package="DIP (Dual Inline) [THT]"]
  28BYJ-48_Stepper_Motor = 28BYJ-48 Stepper Motor
  X1 = X113647 Stepper Driver Board [package=board]

nets:
  N1: R1.Pin_0, IC1.VT
  N2: R1.Pin_1, R2.Pin_0, Raspberry_Pi_1.GIPO4
  GND: R2.Pin_1, Raspberry_Pi_1.GND, IC1.GND, X1.GND
  N3: Raspberry_Pi_1.GIPO5, X1.IN1
  N4: Raspberry_Pi_1.GIPO6, X1.IN2
  N5: Raspberry_Pi_1.GIPO13, X1.IN3
  N6: Raspberry_Pi_1.GIPO19, X1.IN4
  5V: Raspberry_Pi_1.5V, IC1.5V, X1.+V
  N7: 28BYJ-48_Stepper_Motor.BLUE, X1.BLUE
  N8: 28BYJ-48_Stepper_Motor.PINK, X1.PINK
  N9: 28BYJ-48_Stepper_Motor.RED, X1.RED
  N10: 28BYJ-48_Stepper_Motor.ORANGE, X1.ORANGE
  N11: 28BYJ-48_Stepper_Motor.YELLOW, X1.YELLOW

custom parts:
  28BYJ-48 Stepper Motor: 28BYJ-48 gear-reduction stepper motor (small)
  X113647 Stepper Driver Board: A common stepper motor driver board based on ULN2003APG darlington array
